# Fritzing sketch schem (saved by Fritzing 0.9.2b)
circuit board: 8.46667cm x 5.64444cm
breadboards: 1

parts:
  Teensy_3_1 = Teensy 3.1
  C1 = Electrolytic Capacitor [capacitance=1mF voltage=16V package="100 mil [THT, electrolytic]"]
  LED1 = LED - 5mm [color="Red (633nm)" package="5 mm [THT]"]
  S1 = Pushbutton [package=THT]
  S2 = Pushbutton [package=THT]
  TRS1 = Audio Jack (TRS) 3.5mm [package="4Ucon 08780 [THT]"]
  TRS2 = Audio Jack (TRS) 3.5mm [package="4Ucon 08780 [THT]"]
  C2 = Electrolytic Capacitor [capacitance=10µF voltage=50V package="100 mil [THT, electrolytic]"]
  R2 = Resistor [tolerance=±5% resistance=10k package=THT]
  LED2 = LED - 5mm [color="Red (633nm)" package="5 mm [THT]"]
  JP1 = Header 8 [package=1x08_smd]
  JP2 = Header 8 [package=1x08_smd]
  JP3 = Header 6 [package=1x06-smd]
  JP4 = Header 6 [package=1x06-smd]
  JP7 = Header 6 [package=1x06-smd]
  R3 = Resistor [tolerance=±5% resistance=470 package=THT]
  JP8 = Header 6 [package=1x06-smd]
  JP9 = Header 6 [package=1x06-smd]
  JP10 = Header 6 [package=1x06-smd]
  R4 = Resistor [tolerance=±5% resistance=470 package=THT]
  S3 = Pushbutton [package=THT]

nets:
  N1: Teensy_3_1.D2, LED2.anode
  N2: Teensy_3_1.D3, JP1.1, JP1.2, JP1.3, JP1.4, JP1.5, JP1.6, JP1.7, JP1.8
  N3: Teensy_3_1.D4, R3.Pin_0
  N4: Teensy_3_1.D5, R4.Pin_0
  N5: Teensy_3_1.D7, S2.leg0, R2.Pin_0
  N6: Teensy_3_1.3V3, C1.+
  N7: Teensy_3_1.D13, LED1.anode
  N8: Teensy_3_1.A2/D16, C2.-
  GND: Teensy_3_1.AGND, C1.-, LED1.cathode, TRS1.Sleeve, TRS2.Sleeve, R2.Pin_1, LED2.cathode, JP2.1, JP2.2, JP2.3, JP2.4, JP2.5, JP2.6, JP2.7, JP2.8, JP7.1, JP7.2, JP7.3, JP7.4, JP7.5, JP7.6, S3.leg0
  N9: Teensy_3_1.Vin, S1.leg1
  5V: S1.leg0
  3.3V: S2.leg1, JP4.1, JP4.2, JP4.3, JP4.4, JP4.5, JP4.6, JP8.1, JP8.2, JP8.3, JP8.4, JP8.5, JP8.6
  N10: TRS1.Ring, TRS2.Ring
  N11: TRS1.Tip, TRS2.Tip, C2.+
  N12: JP3.1, JP3.2, JP3.3, JP3.4, JP3.5, JP3.6, R3.Pin_1
  N13: JP9.1, JP9.2, JP9.3, JP9.4, JP9.5, JP9.6, R4.Pin_1
  N14: JP10.1, JP10.2, JP10.3, JP10.4, JP10.5, JP10.6, S3.leg1

notes:
  power LED
  mode toggle
  line-in
  input ->
  output ->
  power switch
  bass LED
  bass light extension
  SA extension
  BV extension
  BV toggle
  Extensions are rows of female headers for positive headers to be connected. This allows lights to be added / removed more easily.
